# Fritzing sketch project (saved by Fritzing 0.9.3b)

parts:
  Part1 = Intel Galileo  # not connected
  Raspberry_Pi_1 = Raspberry Pi 3 [part_number=RPI-3-V1.2]
  S1 = H-Bridge with L298N
  M1 = DC Motor
  M2 = DC Motor
  BAT1 = Battery Holders [package=battery-aa]
  BAT2 = Battery Holders [package=battery-aa]
  BAT3 = Battery Holders [package=battery-aa]
  BAT4 = Battery Holders [package=battery-aa]

nets:
  N1: Raspberry_Pi_1.GPIO4, S1.ENA
  N2: Raspberry_Pi_1.GPIO17, S1.IN1
  N3: Raspberry_Pi_1.GPIO27, S1.IN2
  N4: Raspberry_Pi_1.GPIO22, S1.ENB
  GND: Raspberry_Pi_1.GND, S1.GND, BAT4.+
  N5: Raspberry_Pi_1.GPIO23, S1.IN4
  N6: Raspberry_Pi_1.GPIO18, S1.IN3
  N7: S1.12V, BAT1.-
  N8: S1.M1-01, M2.pin_2
  N9: S1.M1-02, M2.pin_1
  N10: S1.M2-01, M1.pin_2
  N11: S1.M2-02, M1.pin_1
  N12: BAT1.+, BAT3.-
  N13: BAT2.-, BAT3.+
  N14: BAT2.+, BAT4.-

custom parts:
  Intel Galileo: Galileo is a microcontroller board based on the Intel® Quark SoC X1000 Application Processor, a 32-bit Intel Pentium-class system on a chip (datasheet). It’s the first board based on Intel® architecture designed to be hardware and software pin-compatible with Arduino shields designed for the Uno R3. Digital pins 0 to 13 (and the adjacent AREF and GND pins), Analog inputs 0 to 5, the power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
  H-Bridge with L298N: h-bridge
